# Fritzing sketch remote (saved by Fritzing 1.0.1rc)
circuit board: 2.09424cm x 3.05769cm
breadboards: 1

parts:
  U1 = ATTINY13 [package=dip]
  C1 = Capacitor [package=cap-pth-small]
  STX882 = mystery part, 3 pins [chip_label=?]
  R1 = Resistor [tolerance=±5% power=0.25 resistance=220 package=THT]
  LED1 = LED - 5mm [color="Red (633nm)" current=0.030 package="5 mm [THT]"]
  S2 = Toggle Switch [package=THT]
  - = mystery part, 2 pins [chip_label=?]

nets:
  N1: U1.PB3(ADC3), STX882.pin1
  N2: U1.GND, C1.1, STX882.pin3, LED1.cathode, S2.COM, -.pin1
  N3: U1.PB0(MOSI), S2.L1
  N4: U1.PB2(SCK_ADC1), R1.Pin_0
  N5: U1.VCC, C1.2, STX882.pin2, -.pin2
  N6: R1.Pin_1, LED1.anode

notes:
  Remote V1
  433MHz
